# Fritzing sketch ultrasonic (saved by Fritzing 0.9.3b)
breadboards: 1

parts:
  Part1 = Arduino Uno (Rev3)
  hc-sr1 = hc-sr04
  LED1 = RGB LED (com. cathode, rbg) [package="5 mm [THT]"]

nets:
  N1: Part1.D9_PWM, LED1.red_anode
  N2: Part1.D11_PWM/MOSI, LED1.green_anode
  N3: Part1.D7, hc-sr1.Trig, hc-sr1.Echo
  5V: Part1.5V, hc-sr1.VCC
  GND: Part1.GND, hc-sr1.GND, LED1.blue_anode
