# Fritzing sketch rgb (saved by Fritzing 0.9.3b)
breadboards: 1

parts:
  Part1 = Arduino Uno (Rev3)
  R1 = Resistor [tolerance=±5% resistance=1k package=THT]
  R2 = PHOTOCELL [package=photocell-kit]
  R3 = Resistor [tolerance=±5% resistance=1k package=THT]
  S1 = Pushbutton [package="[THT]"]
  LED2 = RGB LED (com. cathode, rbg) [package="5 mm [THT]"]

nets:
  N1: Part1.A0, R2.P$2, R3.Pin_1
  N2: Part1.D2, R1.Pin_0, S1.Pin_1, S1.Pin_2
  N3: Part1.D3_PWM, LED2.green_anode
  N4: Part1.D5_PWM, LED2.common_cathode
  N5: Part1.D6_PWM, LED2.red_anode
  N6: Part1.5V, R2.P$1, S1.Pin_3, S1.Pin_4
  N7: Part1.GND, R1.Pin_1, R3.Pin_0, LED2.blue_anode
